// Logisim project 8-BIT-CPU.circ as structural Verilog: 14 circuits, main circuit main
module main (
  input  in_1,
  input  in_2,
  input  RESET,
  output [7:0] out_4,
  output ST,
  output AI,
  output AO,
  output BI,
  output DO,
  output EO,
  output SU,
  output RI,
  output RO,
  output MI,
  output PI,
  output PO,
  output PE,
  output II,
  output IO,
  output FI
);

  wire alu_8_bit_1_out_7, alu_8_bit_1_out_8, alu_8_bit_1_out_9, clock_module_1_out_4;
  wire [2:0] cpu_flags_register_1_out_7;
  wire [3:0] display_module_1_out_5, display_module_1_out_6, display_module_1_out_7, display_module_1_out_8,
       display_module_1_out_9, display_module_1_out_10, display_module_1_out_11, display_module_1_out_12,
       instruction_register_1_out_6, memory_address_register_1_out_5;
  wire [7:0] A_REGISTER_out_6, B_REGISTER_out_6;

  CLOCK_MODULE clock_module_1 (.in_1(in_1), .in_2(in_2), .in_3(ST), .out_4(clock_module_1_out_4));
  REGISTER_8_BIT A_REGISTER (
    .in_2(out_4), .in_1(clock_module_1_out_4), .in_3(RESET), .in_5(AO), .in_4(AI), .out_6(A_REGISTER_out_6),
    .out_7(out_4));
  REGISTER_8_BIT B_REGISTER (
    .in_2(out_4), .in_1(clock_module_1_out_4), .in_3(RESET), .in_4(BI), .out_6(B_REGISTER_out_6));  // open: in_5, out_7
  PROGRAM_COUNTER program_counter_1 (
    .in_1(PI), .in_2(out_4[3:0]), .in_3(PE), .in_4(clock_module_1_out_4), .in_5(RESET), .out_7(out_4[3:0]),
    .in_6(PO));
  ALU_8_BIT alu_8_bit_1 (
    .in_2(B_REGISTER_out_6), .in_3(A_REGISTER_out_6), .out_9(alu_8_bit_1_out_9), .in_4(SU), .out_6(out_4),
    .in_1(EO), .out_8(alu_8_bit_1_out_8), .out_7(alu_8_bit_1_out_7));  // open: out_5
  Pull_Resistor pull_resistor_1 (.node(out_4));
  CPU_FLAGS_REGISTER cpu_flags_register_1 (
    .in_1(clock_module_1_out_4), .in_2(alu_8_bit_1_out_8), .in_3(RESET), .in_4(alu_8_bit_1_out_9),
    .in_5(alu_8_bit_1_out_7), .in_6(FI), .out_7(cpu_flags_register_1_out_7[0]),
    .out_8(cpu_flags_register_1_out_7[1]), .out_9(cpu_flags_register_1_out_7[2]));
  INSTRUCTION_REGISTER instruction_register_1 (
    .in_1(clock_module_1_out_4), .in_2(RESET), .in_3(out_4), .in_4(II), .in_5(IO),
    .out_6(instruction_register_1_out_6), .out_7(out_4[3:0]));
  MEMORY_ADDRESS_REGISTER memory_address_register_1 (
    .in_1(clock_module_1_out_4), .in_2(RESET), .in_3(out_4[3:0]), .in_4(MI),
    .out_5(memory_address_register_1_out_5));
  CONTROL_UNIT control_unit_1 (
    .in_1(cpu_flags_register_1_out_7), .in_2(instruction_register_1_out_6), .in_4(RESET),
    .out_5({ST, AI, AO, BI, DO, EO, SU, RI, RO, MI, PI, PO, PE, II, IO, FI}), .in_3(clock_module_1_out_4));
  RAM_MODULE ram_module_1 (.in_1(memory_address_register_1_out_5), .out_5(out_4), .in_2(out_4), .in_3(RI), .in_4(RO));
  DISPLAY_MODULE display_module_1 (
    .out_9(display_module_1_out_9), .out_10(display_module_1_out_10), .out_11(display_module_1_out_11),
    .out_12(display_module_1_out_12), .out_5(display_module_1_out_5), .out_6(display_module_1_out_6),
    .out_7(display_module_1_out_7), .out_8(display_module_1_out_8), .in_1(DO), .in_4(out_4),
    .in_2(clock_module_1_out_4), .in_3(RESET));
  _7_Segment_Display u_7_segment_display_1 (
    .g(display_module_1_out_5[3]), .f(display_module_1_out_5[2]), .a(display_module_1_out_5[1]),
    .b(display_module_1_out_5[0]), .e(display_module_1_out_12[3]), .d(display_module_1_out_12[2]),
    .c(display_module_1_out_12[1]), .dp(display_module_1_out_12[0]));
  _7_Segment_Display u_7_segment_display_2 (
    .g(display_module_1_out_7[3]), .f(display_module_1_out_7[2]), .a(display_module_1_out_7[1]),
    .b(display_module_1_out_7[0]), .e(display_module_1_out_10[3]), .d(display_module_1_out_10[2]),
    .c(display_module_1_out_10[1]), .dp(display_module_1_out_10[0]));
  _7_Segment_Display u_7_segment_display_3 (
    .g(display_module_1_out_6[3]), .f(display_module_1_out_6[2]), .a(display_module_1_out_6[1]),
    .b(display_module_1_out_6[0]), .e(display_module_1_out_11[3]), .d(display_module_1_out_11[2]),
    .c(display_module_1_out_11[1]), .dp(display_module_1_out_11[0]));
  _7_Segment_Display u_7_segment_display_4 (
    .g(display_module_1_out_8[3]), .f(display_module_1_out_8[2]), .a(display_module_1_out_8[1]),
    .b(display_module_1_out_8[0]), .e(display_module_1_out_9[3]), .d(display_module_1_out_9[2]),
    .c(display_module_1_out_9[1]), .dp(display_module_1_out_9[0]));
endmodule

module REGISTER_1_BIT (
  input  in_1,
  input  in_2,
  input  in_3,
  input  in_4,
  input  in_5,
  output out_6,
  output out_7
);

  Register #(.width(1)) register_1 (.D(in_3), .en(in_4), .Q(out_6), .clk(in_1), .clr(in_2));
  assign out_7 = in_5 ? out_6 : 1'bz;  // Controlled_Buffer controlled_buffer_1
endmodule

module REGISTER_8_BIT (
  input  in_1,
  input  [7:0] in_2,
  input  in_3,
  input  in_4,
  input  in_5,
  output [7:0] out_6,
  output [7:0] out_7
);

  REGISTER_1_BIT register_1_bit_1 (
    .in_3(in_2[7]), .in_4(in_4), .in_1(in_1), .in_2(in_3), .in_5(in_5), .out_6(out_6[7]), .out_7(out_7[7]));
  REGISTER_1_BIT register_1_bit_2 (
    .in_3(in_2[6]), .in_4(in_4), .in_1(in_1), .in_2(in_3), .in_5(in_5), .out_6(out_6[6]), .out_7(out_7[6]));
  REGISTER_1_BIT register_1_bit_3 (
    .in_3(in_2[5]), .in_4(in_4), .in_1(in_1), .in_2(in_3), .in_5(in_5), .out_6(out_6[5]), .out_7(out_7[5]));
  REGISTER_1_BIT register_1_bit_4 (
    .in_3(in_2[4]), .in_4(in_4), .in_1(in_1), .in_2(in_3), .in_5(in_5), .out_6(out_6[4]), .out_7(out_7[4]));
  REGISTER_1_BIT register_1_bit_5 (
    .in_3(in_2[3]), .in_4(in_4), .in_1(in_1), .in_2(in_3), .in_5(in_5), .out_6(out_6[3]), .out_7(out_7[3]));
  REGISTER_1_BIT register_1_bit_6 (
    .in_3(in_2[2]), .in_4(in_4), .in_1(in_1), .in_2(in_3), .in_5(in_5), .out_6(out_6[2]), .out_7(out_7[2]));
  REGISTER_1_BIT register_1_bit_7 (
    .in_3(in_2[1]), .in_4(in_4), .in_1(in_1), .in_2(in_3), .in_5(in_5), .out_6(out_6[1]), .out_7(out_7[1]));
  REGISTER_1_BIT register_1_bit_8 (
    .in_3(in_2[0]), .in_4(in_4), .in_1(in_1), .in_2(in_3), .in_5(in_5), .out_6(out_6[0]), .out_7(out_7[0]));
endmodule

module ALU_1_BIT (
  input  in_1,
  input  in_2,
  input  in_3,
  input  in_4,
  output out_5,
  output out_6
);

  wire xor_1_out;

  Adder #(.width(1)) adder_1 (.a(in_2), .b(xor_1_out), .out(out_5), .cin(in_1), .cout(out_6));
  xor xor_1 (xor_1_out, in_3, in_4);
endmodule

module ALU_8_BIT (
  input  in_1,
  input  [7:0] in_2,
  input  [7:0] in_3,
  input  in_4,
  output [7:0] out_5,
  output [7:0] out_6,
  output out_7,
  output out_8,
  output out_9
);

  wire alu_1_bit_1_out_6, alu_1_bit_2_out_6, alu_1_bit_3_out_6, alu_1_bit_4_out_6, alu_1_bit_5_out_6,
       alu_1_bit_6_out_6, alu_1_bit_7_out_6;

  ALU_1_BIT alu_1_bit_1 (
    .in_2(in_3[0]), .in_3(in_2[0]), .in_4(in_4), .in_1(in_4), .out_5(out_5[0]), .out_6(alu_1_bit_1_out_6));
  ALU_1_BIT alu_1_bit_2 (
    .in_2(in_3[1]), .in_3(in_2[1]), .in_4(in_4), .in_1(alu_1_bit_1_out_6), .out_5(out_5[1]),
    .out_6(alu_1_bit_2_out_6));
  assign out_6 = in_1 ? out_5 : 8'bz;  // Controlled_Buffer controlled_buffer_1
  ALU_1_BIT alu_1_bit_3 (
    .in_2(in_3[2]), .in_3(in_2[2]), .in_4(in_4), .in_1(alu_1_bit_2_out_6), .out_5(out_5[2]),
    .out_6(alu_1_bit_3_out_6));
  nor nor_1 (out_8, out_5[7], out_5[6], out_5[5], out_5[4], out_5[3], out_5[2], out_5[1], out_5[0]);
  ALU_1_BIT alu_1_bit_4 (
    .in_2(in_3[3]), .in_3(in_2[3]), .in_4(in_4), .in_1(alu_1_bit_3_out_6), .out_5(out_5[3]),
    .out_6(alu_1_bit_4_out_6));
  ALU_1_BIT alu_1_bit_5 (
    .in_2(in_3[4]), .in_3(in_2[4]), .in_4(in_4), .in_1(alu_1_bit_4_out_6), .out_5(out_5[4]),
    .out_6(alu_1_bit_5_out_6));
  ALU_1_BIT alu_1_bit_6 (
    .in_2(in_3[5]), .in_3(in_2[5]), .in_4(in_4), .in_1(alu_1_bit_5_out_6), .out_5(out_5[5]),
    .out_6(alu_1_bit_6_out_6));
  ALU_1_BIT alu_1_bit_7 (
    .in_2(in_3[6]), .in_3(in_2[6]), .in_4(in_4), .in_1(alu_1_bit_6_out_6), .out_5(out_5[6]),
    .out_6(alu_1_bit_7_out_6));
  ALU_1_BIT alu_1_bit_8 (
    .in_2(in_3[7]), .in_3(in_2[7]), .in_4(in_4), .in_1(alu_1_bit_7_out_6), .out_5(out_5[7]), .out_6(out_9));

  assign out_7 = out_5[7];
endmodule

module REGISTER_4_BIT (
  input  in_1,
  input  in_2,
  input  [3:0] in_3,
  input  in_4,
  input  in_5,
  output [3:0] out_6,
  output [3:0] out_7
);

  REGISTER_1_BIT register_1_bit_1 (
    .in_3(in_3[0]), .in_4(in_4), .in_1(in_1), .in_2(in_2), .in_5(in_5), .out_6(out_6[0]), .out_7(out_7[0]));
  REGISTER_1_BIT register_1_bit_2 (
    .in_3(in_3[1]), .in_4(in_4), .in_1(in_1), .in_2(in_2), .in_5(in_5), .out_6(out_6[1]), .out_7(out_7[1]));
  REGISTER_1_BIT register_1_bit_3 (
    .in_3(in_3[2]), .in_4(in_4), .in_1(in_1), .in_2(in_2), .in_5(in_5), .out_6(out_6[2]), .out_7(out_7[2]));
  REGISTER_1_BIT register_1_bit_4 (
    .in_3(in_3[3]), .in_4(in_4), .in_1(in_1), .in_2(in_2), .in_5(in_5), .out_6(out_6[3]), .out_7(out_7[3]));
endmodule

module MEMORY_ADDRESS_REGISTER (
  input  in_1,
  input  in_2,
  input  [3:0] in_3,
  input  in_4,
  output [3:0] out_5
);

  REGISTER_4_BIT register_4_bit_1 (
    .in_1(in_1), .in_2(in_2), .in_3(in_3), .in_4(in_4), .out_6(out_5));  // open: in_5, out_7
endmodule

module RAM_MODULE (
  input  [3:0] in_1,
  input  [7:0] in_2,
  input  in_3,
  input  in_4,
  output [7:0] out_5
);

  wire not_1_out;
  wire [7:0] ram_1_data;

  not not_1 (not_1_out, in_3);
  RAM #(.addrWidth(4), .bus("asynch")) ram_1 (.addr(in_1), .data(ram_1_data), .sel(1'b1), .ld(not_1_out), .clr(1'b0));
  assign ram_1_data = in_3 ? in_2 : 8'bz;  // Controlled_Buffer controlled_buffer_1
  assign out_5 = in_4 ? ram_1_data : 8'bz;  // Controlled_Buffer controlled_buffer_2
endmodule

module INSTRUCTION_REGISTER (
  input  in_1,
  input  in_2,
  input  [7:0] in_3,
  input  in_4,
  input  in_5,
  output [3:0] out_6,
  output [3:0] out_7
);

  wire [3:0] register_8_bit_1_out_6;
  wire [7:4] register_8_bit_1_out_7;

  REGISTER_8_BIT register_8_bit_1 (
    .in_2(in_3), .in_1(in_1), .in_3(in_2), .in_5(in_5), .in_4(in_4), .out_6({out_6, register_8_bit_1_out_6}),
    .out_7({register_8_bit_1_out_7, out_7}));
endmodule

module CPU_FLAGS_REGISTER (
  input  in_1,
  input  in_2,
  input  in_3,
  input  in_4,
  input  in_5,
  input  in_6,
  output out_7,
  output out_8,
  output out_9
);

  REGISTER_1_BIT register_1_bit_1 (
    .in_3(in_2), .in_4(in_6), .in_1(in_1), .in_2(in_3), .out_6(out_7));  // open: in_5, out_7
  REGISTER_1_BIT register_1_bit_2 (
    .in_3(in_4), .in_4(in_6), .in_1(in_1), .in_2(in_3), .out_6(out_8));  // open: in_5, out_7
  REGISTER_1_BIT register_1_bit_3 (
    .in_3(in_5), .in_4(in_6), .in_1(in_1), .in_2(in_3), .out_6(out_9));  // open: in_5, out_7
endmodule

module CLOCK_MODULE (
  input  in_1,
  input  in_2,
  input  in_3,
  output out_4
);

  wire and_1_out, and_2_out, clock_1_out, not_1_out, not_2_out, or_1_out;

  Clock clock_1 (.out(clock_1_out));
  and and_1 (and_1_out, in_1, in_2);
  not not_1 (not_1_out, in_2);
  and and_2 (and_2_out, not_1_out, clock_1_out);
  not not_2 (not_2_out, in_3);
  or or_1 (or_1_out, and_1_out, and_2_out);
  and and_3 (out_4, or_1_out, not_2_out);
endmodule

module PROGRAM_COUNTER (
  input  in_1,
  input  [3:0] in_2,
  input  in_3,
  input  in_4,
  input  in_5,
  input  in_6,
  output [3:0] out_7
);

  wire [3:0] counter_1_q;

  Counter #(.width(4), .max('hf)) counter_1 (
    .load(in_1), .D(in_2), .count(in_3), .Q(counter_1_q), .clk(in_4), .clr(in_5));  // open: carry
  assign out_7 = in_6 ? counter_1_q : 4'bz;  // Controlled_Buffer controlled_buffer_1
endmodule

module CONTROL_UNIT (
  input  [2:0] in_1,
  input  [3:0] in_2,
  input  in_3,
  input  in_4,
  output [15:0] out_5
);

  wire and_1_out, not_1_out, not_2_out, or_1_out;
  wire [2:0] counter_1_q;

  not not_1 (not_1_out, in_3);
  Counter #(.width(3), .max('h7)) counter_1 (
    .Q(counter_1_q), .clk(not_1_out), .clr(or_1_out));  // open: load, D, count, carry
  or or_1 (or_1_out, and_1_out, in_4);
  not not_2 (not_2_out, counter_1_q[1]);
  ROM #(.addrWidth(10), .dataWidth(16)) rom_1 (.addr({in_1, in_2, counter_1_q}), .data(out_5), .sel(1'b1));
  and and_1 (and_1_out, counter_1_q[0], not_2_out, counter_1_q[2]);

  // Notes on the sheet:
  //   INSTRUCTION DECODER
  //   contents of rom_1 (hex, n*v repeats v):
  //   50 8c 6*0 50 8c 4002 5*0 50 8c 42 4080 4*0 50 8c 42 2100 4*0 50 8c 42 1080 4401 0 0 0 50 8c 42 1080
  //   4601 0 0 0 50 8c 8000 5*0 50 8c 22 5*0 50 8c 6*0 50 8c 6*0 50 8c 6*0 50 8c 6*0 50 8c 2800 37*0 50 8c
  //   4002 5*0 50 8c 42 4080 4*0 50 8c 42 2100 4*0 50 8c 42 1080 4401 0 0 0 50 8c 42 1080 4601 0 0 0 50 8c
  //   8000 5*0 50 8c 22 5*0 50 8c 6*0 50 8c 6*0 50 8c 22 5*0 50 8c 6*0 50 8c 2800 37*0 50 8c 4002 5*0 50
  //   8c 42 4080 4*0 50 8c 42 2100 4*0 50 8c 42 1080 4401 0 0 0 50 8c 42 1080 4601 0 0 0 50 8c 8000 5*0 50
  //   8c 22 5*0 50 8c 6*0 50 8c 22 5*0 50 8c 6*0 50 8c 6*0 50 8c 2800 37*0 50 8c 4002 5*0 50 8c 42 4080
  //   4*0 50 8c 42 2100 4*0 50 8c 42 1080 4401 0 0 0 50 8c 42 1080 4601 0 0 0 50 8c 8000 5*0 50 8c 22 5*0
  //   50 8c 6*0 50 8c 22 5*0 50 8c 22 5*0 50 8c 6*0 50 8c 2800 37*0 50 8c 4002 5*0 50 8c 42 4080 4*0 50 8c
  //   42 2100 4*0 50 8c 42 1080 4401 0 0 0 50 8c 42 1080 4601 0 0 0 50 8c 8000 5*0 50 8c 22 5*0 50 8c 6*0
  //   50 8c 6*0 50 8c 6*0 50 8c 22 5*0 50 8c 2800 37*0 50 8c 4002 5*0 50 8c 42 4080 4*0 50 8c 42 2100 4*0
  //   50 8c 42 1080 4401 0 0 0 50 8c 42 1080 4601 0 0 0 50 8c 8000 5*0 50 8c 22 5*0 50 8c 6*0 50 8c 6*0 50
  //   8c 22 5*0 50 8c 22 5*0 50 8c 2800 37*0 50 8c 4002 5*0 50 8c 42 4080 4*0 50 8c 42 2100 4*0 50 8c 42
  //   1080 4401 0 0 0 50 8c 42 1080 4601 0 0 0 50 8c 8000 5*0 50 8c 22 5*0 50 8c 6*0 50 8c 22 5*0 50 8c
  //   6*0 50 8c 22 5*0 50 8c 2800 37*0 50 8c 4002 5*0 50 8c 42 4080 4*0 50 8c 42 2100 4*0 50 8c 42 1080
  //   4401 0 0 0 50 8c 42 1080 4601 0 0 0 50 8c 8000 5*0 50 8c 22 5*0 50 8c 6*0 50 8c 22 5*0 50 8c 22 5*0
  //   50 8c 22 5*0 50 8c 2800
endmodule

module DISPLAY_MODULE (
  input  in_1,
  input  in_2,
  input  in_3,
  input  [7:0] in_4,
  output [3:0] out_5,
  output [3:0] out_6,
  output [3:0] out_7,
  output [3:0] out_8,
  output [3:0] out_9,
  output [3:0] out_10,
  output [3:0] out_11,
  output [3:0] out_12
);

  wire [7:0] register_1_q;

  and and_1 (out_5[3], register_1_q[7], 1'b0);
  ROM #(.addrWidth(9)) rom_1 (
    .addr({1'b0, register_1_q}), .data({out_11[0], out_11[1], out_11[2], out_11[3], out_6}), .sel(1'b1));
  ROM #(.addrWidth(9)) rom_2 (
    .addr({1'b0, register_1_q}), .data({out_10[0], out_10[1], out_10[2], out_10[3], out_7}), .sel(1'b1));
  ROM #(.addrWidth(9)) rom_3 (
    .addr({1'b0, register_1_q}), .data({out_9[0], out_9[1], out_9[2], out_9[3], out_8}), .sel(1'b1));
  Register register_1 (.D(in_4), .en(in_1), .Q(register_1_q), .clk(in_2), .clr(in_3));

  // Notes on the sheet:
  //   contents of rom_1 (hex, n*v repeats v):
  //   100*77 100*41 56*3b 100*77 57*41 99*77
  //   contents of rom_2 (hex, n*v repeats v):
  //   10*77 10*41 10*3b 10*6b 10*4d 10*6e 10*7e 10*43 10*7f 10*6f 10*77 10*41 10*3b 10*6b 10*4d 10*6e
  //   10*7e 10*43 10*7f 10*6f 10*77 10*41 10*3b 10*6b 10*4d 6*6e 10*77 10*41 10*3b 10*6b 10*4d 10*6e 10*7e
  //   10*43 10*7f 10*6f 10*77 10*41 17*3b 10*41 10*77 10*6f 10*7f 10*43 10*7e 10*6e 10*4d 10*6b 10*3b
  //   10*41 9*77
  //   contents of rom_3 (hex, n*v repeats v):
  //   77 41 3b 6b 4d 6e 7e 43 7f 6f 77 41 3b 6b 4d 6e 7e 43 7f 6f 77 41 3b 6b 4d 6e 7e 43 7f 6f 77 41 3b
  //   6b 4d 6e 7e 43 7f 6f 77 41 3b 6b 4d 6e 7e 43 7f 6f 77 41 3b 6b 4d 6e 7e 43 7f 6f 77 41 3b 6b 4d 6e
  //   7e 43 7f 6f 77 41 3b 6b 4d 6e 7e 43 7f 6f 77 41 3b 6b 4d 6e 7e 43 7f 6f 77 41 3b 6b 4d 6e 7e 43 7f
  //   6f 77 41 3b 6b 4d 6e 7e 43 7f 6f 77 41 3b 6b 4d 6e 7e 43 7f 6f 77 41 3b 6b 4d 6e 7e 43 7f 6f 77 41
  //   3b 6b 4d 6e 7e 43 7f 6f 77 41 3b 6b 4d 6e 7e 43 7f 6f 77 41 3b 6b 4d 6e 7e 43 7f 6f 77 41 3b 6b 4d
  //   6e 7e 43 7f 6f 77 41 3b 6b 4d 6e 7e 43 7f 6f 77 41 3b 6b 4d 6e 7e 43 7f 6f 77 41 3b 6b 4d 6e 7e 43
  //   7f 6f 77 41 3b 6b 4d 6e 7e 43 7f 6f 77 41 3b 6b 4d 6e 7e 43 7f 6f 77 41 3b 6b 4d 6e 7e 43 7f 6f 77
  //   41 3b 6b 4d 6e 7e 43 7f 6f 77 41 3b 6b 4d 6e 7e 43 7f 6f 77 41 3b 6b 4d 6e 77 41 3b 6b 4d 6e 7e 43
  //   7f 6f 77 41 3b 6b 4d 6e 7e 43 7f 6f 77 41 3b 6b 4d 6e 7e 43 7f 6f 77 41 3b 6b 4d 6e 7e 43 7f 6f 77
  //   41 3b 6b 4d 6e 7e 43 7f 6f 77 41 3b 6b 4d 6e 7e 43 7f 6f 77 41 3b 6b 4d 6e 7e 43 7f 6f 77 41 3b 6b
  //   4d 6e 7e 43 7f 6f 77 41 3b 6b 4d 6e 7e 43 7f 6f 77 41 3b 6b 4d 6e 7e 43 7f 6f 77 41 3b 6b 4d 6e 7e
  //   43 7f 6f 77 41 3b 6b 4d 6e 7e 43 7f 6f 77 41 3b 6b 4d 6e 7e 43 7f 43 7e 6e 4d 6b 3b 41 77 6f 7f 43
  //   7e 6e 4d 6b 3b 41 77 6f 7f 43 7e 6e 4d 6b 3b 41 77 6f 7f 43 7e 6e 4d 6b 3b 41 77 6f 7f 43 7e 6e 4d
  //   6b 3b 41 77 6f 7f 43 7e 6e 4d 6b 3b 41 77 6f 7f 43 7e 6e 4d 6b 3b 41 77 6f 7f 43 7e 6e 4d 6b 3b 41
  //   77 6f 7f 43 7e 6e 4d 6b 3b 41 77 6f 7f 43 7e 6e 4d 6b 3b 41 77 6f 7f 43 7e 6e 4d 6b 3b 41 77 6f 7f
  //   43 7e 6e 4d 6b 3b 41 77 6f 7f 43 7e 6e 4d 6b 3b 41
endmodule
