// Logisim project 8-bit-cpu-split-bus.circ as structural Verilog: 11 circuits, main circuit main
module main (
  input  in_1,
  input  in_2,
  input  in_3
);

  wire clock_module_1_out_4, n8_bit_alu_1_out_5, n8_bit_alu_1_out_7, n8_bit_alu_1_out_9;
  wire [2:0] cpu_flags_register_1_out_7;
  wire [3:0] display_module_1_out_5, display_module_1_out_6, display_module_1_out_7, display_module_1_out_8,
       display_module_1_out_9, display_module_1_out_10, display_module_1_out_11, display_module_1_out_12,
       instruction_register_1_out_7;
  wire [7:0] memory_address_register_1_out_5, n8_bit_register_1_out_6, n8_bit_register_1_out_7,
       n8_bit_register_2_out_6, program_counter_1_out_7;
  wire [11:0] ram_module_1_out_6;
  wire [17:0] control_unit_1_out_5;

  CLOCK_MODULE clock_module_1 (.in_1(in_1), .in_2(in_2), .in_3(control_unit_1_out_5[17]), .out_4(clock_module_1_out_4));
  _8_BIT_REGISTER u_8_bit_register_1 (
    .in_1(n8_bit_register_1_out_7), .in_2(control_unit_1_out_5[16]), .in_3(clock_module_1_out_4),
    .in_4(in_3), .in_5(control_unit_1_out_5[15]), .out_7(n8_bit_register_1_out_7),
    .out_6(n8_bit_register_1_out_6));
  _8_BIT_REGISTER u_8_bit_register_2 (
    .in_1(n8_bit_register_1_out_7), .in_2(control_unit_1_out_5[14]), .in_3(clock_module_1_out_4),
    .in_4(in_3), .out_6(n8_bit_register_2_out_6));  // open: in_5, out_7
  _8_BIT_ALU u_8_bit_alu_1 (
    .in_1(n8_bit_register_1_out_6), .in_2(n8_bit_register_2_out_6), .in_3(control_unit_1_out_5[13]),
    .in_4(control_unit_1_out_5[12]), .out_5(n8_bit_alu_1_out_5), .out_7(n8_bit_alu_1_out_7),
    .out_8(n8_bit_register_1_out_7), .out_9(n8_bit_alu_1_out_9));  // open: out_6
  CPU_FLAGS_REGISTER cpu_flags_register_1 (
    .in_1(n8_bit_alu_1_out_5), .in_2(n8_bit_alu_1_out_7), .in_3(n8_bit_alu_1_out_9),
    .in_4(control_unit_1_out_5[4]), .in_5(clock_module_1_out_4), .in_6(in_3),
    .out_7(cpu_flags_register_1_out_7));
  PROGRAM_COUNTER program_counter_1 (
    .in_1(control_unit_1_out_5[11]), .out_7(program_counter_1_out_7), .in_2(program_counter_1_out_7),
    .in_3(control_unit_1_out_5[10]), .in_4(clock_module_1_out_4), .in_5(in_3), .in_6(control_unit_1_out_5[9]));
  INSTRUCTION_REGISTER instruction_register_1 (
    .in_1(ram_module_1_out_6), .in_2(control_unit_1_out_5[8]), .in_3(clock_module_1_out_4), .in_5(in_3),
    .out_7(instruction_register_1_out_7), .out_8(n8_bit_register_1_out_7), .out_9(program_counter_1_out_7),
    .in_6(control_unit_1_out_5[7]), .in_4(control_unit_1_out_5[6]));
  MEMORY_ADDRESS_REGISTER memory_address_register_1 (
    .in_1(program_counter_1_out_7), .in_2(control_unit_1_out_5[5]), .in_3(clock_module_1_out_4), .in_4(in_3),
    .out_5(memory_address_register_1_out_5));
  DISPLAY_MODULE display_module_1 (
    .out_5(display_module_1_out_5), .out_6(display_module_1_out_6), .out_7(display_module_1_out_7),
    .out_8(display_module_1_out_8), .out_9(display_module_1_out_9), .out_10(display_module_1_out_10),
    .out_11(display_module_1_out_11), .out_12(display_module_1_out_12), .in_1(control_unit_1_out_5[3]),
    .in_4(n8_bit_register_1_out_7), .in_2(clock_module_1_out_4), .in_3(in_3));
  RAM_MODULE ram_module_1 (
    .in_3(memory_address_register_1_out_5), .in_4(n8_bit_register_1_out_7), .in_5(control_unit_1_out_5[2]),
    .out_6(ram_module_1_out_6), .in_1(control_unit_1_out_5[0]), .in_2(control_unit_1_out_5[1]),
    .out_7(n8_bit_register_1_out_7));
  _7_Segment_Display u_7_segment_display_1 (
    .g(display_module_1_out_5[3]), .f(display_module_1_out_5[2]), .a(display_module_1_out_5[1]),
    .b(display_module_1_out_5[0]), .e(display_module_1_out_12[3]), .d(display_module_1_out_12[2]),
    .c(display_module_1_out_12[1]), .dp(display_module_1_out_12[0]));
  CONTROL_UNIT control_unit_1 (
    .in_1(cpu_flags_register_1_out_7), .in_2(instruction_register_1_out_7), .in_3(clock_module_1_out_4),
    .in_4(in_3), .out_5(control_unit_1_out_5));
  _7_Segment_Display u_7_segment_display_2 (
    .g(display_module_1_out_6[3]), .f(display_module_1_out_6[2]), .a(display_module_1_out_6[1]),
    .b(display_module_1_out_6[0]), .e(display_module_1_out_11[3]), .d(display_module_1_out_11[2]),
    .c(display_module_1_out_11[1]), .dp(display_module_1_out_11[0]));
  _7_Segment_Display u_7_segment_display_3 (
    .g(display_module_1_out_7[3]), .f(display_module_1_out_7[2]), .a(display_module_1_out_7[1]),
    .b(display_module_1_out_7[0]), .e(display_module_1_out_10[3]), .d(display_module_1_out_10[2]),
    .c(display_module_1_out_10[1]), .dp(display_module_1_out_10[0]));
  _7_Segment_Display u_7_segment_display_4 (
    .g(display_module_1_out_8[3]), .f(display_module_1_out_8[2]), .a(display_module_1_out_8[1]),
    .b(display_module_1_out_8[0]), .e(display_module_1_out_9[3]), .d(display_module_1_out_9[2]),
    .c(display_module_1_out_9[1]), .dp(display_module_1_out_9[0]));
endmodule

module _8_BIT_REGISTER (
  input  [7:0] in_1,
  input  in_2,
  input  in_3,
  input  in_4,
  input  in_5,
  output [7:0] out_6,
  output [7:0] out_7
);

  Register register_1 (.D(in_1), .en(in_2), .Q(out_6), .clk(in_3), .clr(in_4));
  assign out_7 = in_5 ? out_6 : 8'bz;  // Controlled_Buffer controlled_buffer_1
endmodule

module CLOCK_MODULE (
  input  in_1,
  input  in_2,
  input  in_3,
  output out_4
);

  wire and_1_out, and_2_out, clock_1_out, not_1_out, not_2_out, or_1_out;

  Clock clock_1 (.out(clock_1_out));
  and and_1 (and_1_out, in_1, in_2);
  not not_1 (not_1_out, in_2);
  and and_2 (and_2_out, not_1_out, clock_1_out);
  not not_2 (not_2_out, in_3);
  or or_1 (or_1_out, and_1_out, and_2_out);
  and and_3 (out_4, or_1_out, not_2_out);
endmodule

module PROGRAM_COUNTER (
  input  in_1,
  input  [7:0] in_2,
  input  in_3,
  input  in_4,
  input  in_5,
  input  in_6,
  output [7:0] out_7
);

  wire [7:0] counter_1_q;

  Counter counter_1 (.load(in_1), .D(in_2), .count(in_3), .Q(counter_1_q), .clk(in_4), .clr(in_5));  // open: carry
  assign out_7 = in_6 ? counter_1_q : 8'bz;  // Controlled_Buffer controlled_buffer_1
endmodule

module _8_BIT_ALU (
  input  [7:0] in_1,
  input  [7:0] in_2,
  input  in_3,
  input  in_4,
  output out_5,
  output [7:0] out_6,
  output out_7,
  output [7:0] out_8,
  output out_9
);

  wire [7:0] adder_1_out, demultiplexer_1_out0, demultiplexer_1_out1, demultiplexer_2_out0,
       demultiplexer_2_out1, subtractor_1_out;

  Demultiplexer #(.width(8)) demultiplexer_1 (
    .out0(demultiplexer_1_out0), .out1(demultiplexer_1_out1), .in(in_1), .sel(in_3), .en(1'b1));
  Demultiplexer #(.width(8)) demultiplexer_2 (
    .out0(demultiplexer_2_out0), .out1(demultiplexer_2_out1), .in(in_2), .sel(in_3), .en(1'b1));
  Adder adder_1 (.a(demultiplexer_1_out0), .b(demultiplexer_2_out0), .out(adder_1_out), .cin(1'b0), .cout(out_7));
  Subtractor subtractor_1 (
    .a(demultiplexer_1_out1), .b(demultiplexer_2_out1), .out(subtractor_1_out), .bin(1'b0), .bout(out_9));
  Multiplexer #(.width(8)) multiplexer_1 (
    .in0(adder_1_out), .in1(subtractor_1_out), .out(out_6), .sel(in_3), .en(1'b1));
  assign out_8 = in_4 ? out_6 : 8'bz;  // Controlled_Buffer controlled_buffer_1
  nor nor_1 (out_5, out_6[0], out_6[1], out_6[2], out_6[3], out_6[4], out_6[5], out_6[6], out_6[7]);
endmodule

module RAM_MODULE (
  input  in_1,
  input  in_2,
  input  [7:0] in_3,
  input  [7:0] in_4,
  input  in_5,
  output [11:0] out_6,
  output [7:0] out_7
);

  wire and_1_out, and_2_out, not_1_out, not_2_out;
  wire [11:0] demultiplexer_1_out0, demultiplexer_1_out1, ram_1_data;
  wire [11:8] controlled_buffer_2_out;

  not not_1 (not_1_out, in_5);
  RAM #(.dataWidth(12), .bus("asynch")) ram_1 (.addr(in_3), .data(ram_1_data), .sel(1'b1), .ld(not_1_out), .clr(1'b0));
  assign ram_1_data[7:0] = in_5 ? in_4 : 8'bz;  // Controlled_Buffer controlled_buffer_1
  not not_2 (not_2_out, in_1);
  and and_1 (and_1_out, not_2_out, in_2);
  and and_2 (and_2_out, in_2, in_1);
  Demultiplexer #(.width(12)) demultiplexer_1 (
    .out0(demultiplexer_1_out0), .out1(demultiplexer_1_out1), .in(ram_1_data), .sel(in_1), .en(1'b1));
  assign {controlled_buffer_2_out, out_7} = and_1_out ? demultiplexer_1_out0 : 12'bz;  // Controlled_Buffer controlled_buffer_2
  assign out_6 = and_2_out ? demultiplexer_1_out1 : 12'bz;  // Controlled_Buffer controlled_buffer_3
endmodule

module MEMORY_ADDRESS_REGISTER (
  input  [7:0] in_1,
  input  in_2,
  input  in_3,
  input  in_4,
  output [7:0] out_5
);

  _8_BIT_REGISTER u_8_bit_register_1 (
    .in_1(in_1), .in_2(in_2), .in_3(in_3), .in_4(in_4), .in_5(1'b1), .out_6(out_5));  // open: out_7
endmodule

module INSTRUCTION_REGISTER (
  input  [11:0] in_1,
  input  in_2,
  input  in_3,
  input  in_4,
  input  in_5,
  input  in_6,
  output [3:0] out_7,
  output [7:0] out_8,
  output [7:0] out_9
);

  wire and_1_out, and_2_out, not_1_out;
  wire [7:0] controlled_buffer_1_out, demultiplexer_1_out0, demultiplexer_1_out1, register_1_q;

  Register #(.width(12)) register_1 (.D(in_1), .en(in_2), .Q({out_7, register_1_q}), .clk(in_3), .clr(in_5));
  assign controlled_buffer_1_out = in_6 ? register_1_q : 8'bz;  // Controlled_Buffer controlled_buffer_1
  Demultiplexer #(.width(8)) demultiplexer_1 (
    .out0(demultiplexer_1_out0), .out1(demultiplexer_1_out1), .in(controlled_buffer_1_out), .sel(in_4),
    .en(1'b1));
  and and_1 (and_1_out, in_6, not_1_out);
  not not_1 (not_1_out, in_4);
  and and_2 (and_2_out, in_4, in_6);
  assign out_8 = and_1_out ? demultiplexer_1_out0 : 8'bz;  // Controlled_Buffer controlled_buffer_2
  assign out_9 = and_2_out ? demultiplexer_1_out1 : 8'bz;  // Controlled_Buffer controlled_buffer_3
endmodule

module CPU_FLAGS_REGISTER (
  input  in_1,
  input  in_2,
  input  in_3,
  input  in_4,
  input  in_5,
  input  in_6,
  output [2:0] out_7
);

  Register #(.width(3)) register_1 (.D({in_3, in_2, in_1}), .en(in_4), .Q(out_7), .clk(in_5), .clr(in_6));
endmodule

module CONTROL_UNIT (
  input  [2:0] in_1,
  input  [3:0] in_2,
  input  in_3,
  input  in_4,
  output [17:0] out_5
);

  wire and_1_out, not_1_out, not_2_out, or_1_out;
  wire [2:0] counter_1_q;

  not not_1 (not_1_out, in_3);
  Counter #(.width(3), .max('h7)) counter_1 (
    .Q(counter_1_q), .clk(not_1_out), .clr(or_1_out));  // open: load, D, count, carry
  or or_1 (or_1_out, and_1_out, in_4);
  not not_2 (not_2_out, counter_1_q[1]);
  and and_1 (and_1_out, counter_1_q[0], not_2_out, counter_1_q[2]);
  ROM #(.addrWidth(10), .dataWidth(18)) rom_1 (.addr({in_1, in_2, counter_1_q}), .data(out_5), .sel(1'b1));

  // Notes on the sheet:
  //   INSTRUCTION DECODER
endmodule

module DISPLAY_MODULE (
  input  in_1,
  input  in_2,
  input  in_3,
  input  [7:0] in_4,
  output [3:0] out_5,
  output [3:0] out_6,
  output [3:0] out_7,
  output [3:0] out_8,
  output [3:0] out_9,
  output [3:0] out_10,
  output [3:0] out_11,
  output [3:0] out_12
);

  wire [7:0] register_1_q;

  and and_1 (out_5[3], register_1_q[7], 1'b0);
  ROM #(.addrWidth(9)) rom_1 (
    .addr({1'b0, register_1_q}), .data({out_11[0], out_11[1], out_11[2], out_11[3], out_6}), .sel(1'b1));
  ROM #(.addrWidth(9)) rom_2 (
    .addr({1'b0, register_1_q}), .data({out_10[0], out_10[1], out_10[2], out_10[3], out_7}), .sel(1'b1));
  ROM #(.addrWidth(9)) rom_3 (
    .addr({1'b0, register_1_q}), .data({out_9[0], out_9[1], out_9[2], out_9[3], out_8}), .sel(1'b1));
  Register register_1 (.D(in_4), .en(in_1), .Q(register_1_q), .clk(in_2), .clr(in_3));

  // Notes on the sheet:
  //   contents of rom_1 (hex, n*v repeats v):
  //   100*77 100*41 56*3b 100*77 57*41 99*77
  //   contents of rom_2 (hex, n*v repeats v):
  //   10*77 10*41 10*3b 10*6b 10*4d 10*6e 10*7e 10*43 10*7f 10*6f 10*77 10*41 10*3b 10*6b 10*4d 10*6e
  //   10*7e 10*43 10*7f 10*6f 10*77 10*41 10*3b 10*6b 10*4d 6*6e 10*77 10*41 10*3b 10*6b 10*4d 10*6e 10*7e
  //   10*43 10*7f 10*6f 10*77 10*41 17*3b 10*41 10*77 10*6f 10*7f 10*43 10*7e 10*6e 10*4d 10*6b 10*3b
  //   10*41 9*77
  //   contents of rom_3 (hex, n*v repeats v):
  //   77 41 3b 6b 4d 6e 7e 43 7f 6f 77 41 3b 6b 4d 6e 7e 43 7f 6f 77 41 3b 6b 4d 6e 7e 43 7f 6f 77 41 3b
  //   6b 4d 6e 7e 43 7f 6f 77 41 3b 6b 4d 6e 7e 43 7f 6f 77 41 3b 6b 4d 6e 7e 43 7f 6f 77 41 3b 6b 4d 6e
  //   7e 43 7f 6f 77 41 3b 6b 4d 6e 7e 43 7f 6f 77 41 3b 6b 4d 6e 7e 43 7f 6f 77 41 3b 6b 4d 6e 7e 43 7f
  //   6f 77 41 3b 6b 4d 6e 7e 43 7f 6f 77 41 3b 6b 4d 6e 7e 43 7f 6f 77 41 3b 6b 4d 6e 7e 43 7f 6f 77 41
  //   3b 6b 4d 6e 7e 43 7f 6f 77 41 3b 6b 4d 6e 7e 43 7f 6f 77 41 3b 6b 4d 6e 7e 43 7f 6f 77 41 3b 6b 4d
  //   6e 7e 43 7f 6f 77 41 3b 6b 4d 6e 7e 43 7f 6f 77 41 3b 6b 4d 6e 7e 43 7f 6f 77 41 3b 6b 4d 6e 7e 43
  //   7f 6f 77 41 3b 6b 4d 6e 7e 43 7f 6f 77 41 3b 6b 4d 6e 7e 43 7f 6f 77 41 3b 6b 4d 6e 7e 43 7f 6f 77
  //   41 3b 6b 4d 6e 7e 43 7f 6f 77 41 3b 6b 4d 6e 7e 43 7f 6f 77 41 3b 6b 4d 6e 77 41 3b 6b 4d 6e 7e 43
  //   7f 6f 77 41 3b 6b 4d 6e 7e 43 7f 6f 77 41 3b 6b 4d 6e 7e 43 7f 6f 77 41 3b 6b 4d 6e 7e 43 7f 6f 77
  //   41 3b 6b 4d 6e 7e 43 7f 6f 77 41 3b 6b 4d 6e 7e 43 7f 6f 77 41 3b 6b 4d 6e 7e 43 7f 6f 77 41 3b 6b
  //   4d 6e 7e 43 7f 6f 77 41 3b 6b 4d 6e 7e 43 7f 6f 77 41 3b 6b 4d 6e 7e 43 7f 6f 77 41 3b 6b 4d 6e 7e
  //   43 7f 6f 77 41 3b 6b 4d 6e 7e 43 7f 6f 77 41 3b 6b 4d 6e 7e 43 7f 43 7e 6e 4d 6b 3b 41 77 6f 7f 43
  //   7e 6e 4d 6b 3b 41 77 6f 7f 43 7e 6e 4d 6b 3b 41 77 6f 7f 43 7e 6e 4d 6b 3b 41 77 6f 7f 43 7e 6e 4d
  //   6b 3b 41 77 6f 7f 43 7e 6e 4d 6b 3b 41 77 6f 7f 43 7e 6e 4d 6b 3b 41 77 6f 7f 43 7e 6e 4d 6b 3b 41
  //   77 6f 7f 43 7e 6e 4d 6b 3b 41 77 6f 7f 43 7e 6e 4d 6b 3b 41 77 6f 7f 43 7e 6e 4d 6b 3b 41 77 6f 7f
  //   43 7e 6e 4d 6b 3b 41 77 6f 7f 43 7e 6e 4d 6b 3b 41
endmodule
